# Fritzing sketch B1 (saved by Fritzing 0.9.6b)
circuit board: 8.46667cm x 5.64444cm
breadboards: 1

parts:
  7_Segment1 = 7 Segment Display
  7_Segment2 = 7 Segment Display
  LED1 = smd LED [color="Red (633nm)" package="1206 [SMD]"]
  LED2 = smd LED [color="Green (570nm)" package="1206 [SMD]"]
  LED3 = smd LED [color="Yellow (585nm)" package="1206 [SMD]"]
  R1 = Resistor [tolerance=±5% resistance=100 package="0402 [SMD]"]
  R2 = Resistor [tolerance=±5% resistance=100 package="0402 [SMD]"]
  R3 = Resistor [tolerance=±5% resistance=100 package="0402 [SMD]"]
  R4 = Resistor [tolerance=±5% resistance=100 package="0402 [SMD]"]
  R5 = Resistor [tolerance=±5% resistance=100 package="0402 [SMD]"]
  R6 = Resistor [tolerance=±5% resistance=100 package="0402 [SMD]"]
  R7 = Resistor [tolerance=±5% resistance=100 package="0402 [SMD]"]
  R8 = Resistor [tolerance=±5% resistance=100 package="0402 [SMD]"]
  R10 = Resistor [tolerance=±5% resistance=100 package="0402 [SMD]"]
  R11 = Resistor [tolerance=±5% resistance=100 package="0402 [SMD]"]
  R12 = Resistor [tolerance=±5% resistance=100 package="0402 [SMD]"]
  R13 = Resistor [tolerance=±5% resistance=100 package="0402 [SMD]"]
  R14 = Resistor [tolerance=±5% resistance=100 package="0402 [SMD]"]
  R15 = Resistor [tolerance=±5% resistance=100 package="0402 [SMD]"]
  R16 = Resistor [tolerance=±5% resistance=100 package="0402 [SMD]"]
  R17 = Resistor [tolerance=±5% resistance=100 package="0402 [SMD]"]
  R18 = Resistor [tolerance=±5% resistance=100 package="0402 [SMD]"]
  Raspberry_Pi_1 = Raspberry Pi 3 [part_number=RPI-3-V1.2]
  S1 = Pushbutton [package="[THT]"]
  R19 = Resistor [tolerance=±5% power=0.25 resistance=10k package=THT]

nets:
  N1: 7_Segment1.Segment_E, R11.Pin_0
  N2: 7_Segment1.Segment_D, R10.Pin_0
  N3: 7_Segment1.common_cathode, 7_Segment2.common_cathode, R1.Pin_1, R2.Pin_1, Raspberry_Pi_1.GND, R19.Pin_0
  N4: 7_Segment1.Segment_C, R8.Pin_1
  N5: 7_Segment1.Segment_B, R5.Pin_1
  N6: 7_Segment1.Segment_A, R4.Pin_1
  N7: 7_Segment1.Segment_F, R6.Pin_0
  N8: 7_Segment1.Segment_G, R7.Pin_0
  N9: 7_Segment2.Segment_E, R14.Pin_0
  N10: 7_Segment2.Segment_D, R13.Pin_0
  N11: 7_Segment2.Segment_C, R12.Pin_1
  N12: 7_Segment2.Segment_B, R16.Pin_1
  N13: 7_Segment2.Segment_A, R15.Pin_1
  N14: 7_Segment2.Segment_F, R17.Pin_0
  N15: 7_Segment2.Segment_G, R18.Pin_0
  N16: LED1.cathode, R1.Pin_0
  N17: LED1.anode, Raspberry_Pi_1.GPIO20
  N18: LED2.cathode, R3.Pin_0
  N19: LED2.anode, Raspberry_Pi_1.GPIO26
  N20: LED3.cathode, R2.Pin_0
  N21: LED3.anode, Raspberry_Pi_1.GPIO21
  N22: R4.Pin_0, Raspberry_Pi_1.GPIO17
  N23: R5.Pin_0, Raspberry_Pi_1.GPIO27
  N24: R6.Pin_1, Raspberry_Pi_1.GPIO14
  N25: R8.Pin_0, Raspberry_Pi_1.GPIO23
  N26: R10.Pin_1, Raspberry_Pi_1.GPIO15
  N27: R11.Pin_1, Raspberry_Pi_1.GPIO18
  N28: R12.Pin_0, Raspberry_Pi_1.GPIO16
  N29: R13.Pin_1, Raspberry_Pi_1.GPIO24
  N30: R14.Pin_1, Raspberry_Pi_1.GPIO25
  N31: R15.Pin_0, Raspberry_Pi_1.GPIO5
  N32: R16.Pin_0, Raspberry_Pi_1.GPIO13
  N33: R17.Pin_1, Raspberry_Pi_1.GPIO11
  N34: R18.Pin_1, Raspberry_Pi_1.GPIO9
  N35: Raspberry_Pi_1.3v3, S1.Pin_3, S1.Pin_4
  N36: Raspberry_Pi_1.GPIO19, S1.Pin_1, S1.Pin_2
