# Fritzing sketch B6 (saved by Fritzing 0.9.3b)
breadboards: 1

parts:
  R1 = Resistor [tolerance=±5% resistance=100 package=THT]
  R2 = Resistor [tolerance=±5% resistance=100 package=THT]
  R3 = Resistor [tolerance=±5% resistance=100 package=THT]
  LED1 = smd LED [color="Blue (430nm)" package="0603 [SMD]"]
  LED2 = smd LED [color="Blue (430nm)" package="0603 [SMD]"]
  LED3 = smd LED [color="Blue (430nm)" package="0603 [SMD]"]
  Raspberry_Pi_1 = Raspberry Pi 3 [part_number=RPI-3-V1.2]
  S1 = Pushbutton [package="[SMD]"]
  S2 = Pushbutton [package="[SMD]"]
  R5 = Resistor [tolerance=±5% resistance=10k package=THT]
  R4 = Resistor [tolerance=±5% resistance=10k package=THT]

nets:
  N1: R1.Pin_0, LED1.cathode
  N2: R1.Pin_1, R2.Pin_1, R3.Pin_1, Raspberry_Pi_1.GND, R5.Pin_0, R4.Pin_0
  N3: R2.Pin_0, LED2.cathode
  N4: R3.Pin_0, LED3.cathode
  N5: LED1.anode, Raspberry_Pi_1.GPIO24
  N6: LED2.anode, Raspberry_Pi_1.GPIO18
  N7: LED3.anode, Raspberry_Pi_1.GPIO23
  N8: Raspberry_Pi_1.3v3, S1.Pin_3, S1.Pin_4, S2.Pin_3, S2.Pin_4
  N9: Raspberry_Pi_1.GPIO4, S2.Pin_1, S2.Pin_2, R5.Pin_1
  N10: Raspberry_Pi_1.GPIO15, S1.Pin_1, S1.Pin_2, R4.Pin_1
